# Fritzing sketch OpenMQTTgateway_Arduino_Addon_BT (saved by Fritzing 0.9.3b)
breadboards: 1

parts:
  V1 = DC Power [voltage=5]  # not connected
  Composant1 = Bluetooth HM-10
  Bauteil1 = Arduino Uno (Rev3)

nets:
  N1: Composant1.RXD, Bauteil1.D6_PWM
  N2: Composant1.TXD, Bauteil1.D5_PWM
  GND: Composant1.GND, Bauteil1.GND
  VCC: Composant1.VCC, Bauteil1.5V
