# Fritzing sketch OpenMQTTgateway_Arduino_Addon_DHT (saved by Fritzing 0.9.3b)
breadboards: 1

parts:
  V1 = DC Power [voltage=5]  # not connected
  RHT1 = Humidity and Temperature Sensor RHT03
  Bauteil1 = Arduino Uno (Rev3)

nets:
  VCC: RHT1.Vcc, Bauteil1.5V
  N1: RHT1.Data-signal, Bauteil1.D8
  N2: RHT1.GND_2, Bauteil1.GND
