# Fritzing sketch OpenMQTTgateway_ESP32_Addon_IR (saved by Fritzing 0.9.3b)
breadboards: 1

parts:
  V1 = DC Power [voltage=5]
  R2 = Resistor [tolerance=±5% resistance=330 package="2512 [SMD]"]
  Q1 = TRANSISTOR_NPN [package=to-92-ammo]
  IR2 = TSOP312.., 314.. [package=THT]
  R5 = Resistor [tolerance=±5% resistance=220 package="2512 [SMD]"]
  LED2 = LEDs [package=led10mm]
  Composant2 = Adafruit HUZZAH32 ESP32 Feather [part_number="Adafruit #3405"]

nets:
  N1: V1.V+, IR2.Vs, LED2.C, Composant2.VBUS
  N2: R2.Pin_0, Composant2.IO14_A6
  N3: R2.Pin_1, Q1.B
  N4: Q1.E, R5.Pin_1
  GND: Q1.C, IR2.GND, Composant2.GND
  N5: IR2.Data, Composant2.IO33_A9
  N6: R5.Pin_0, LED2.A
