# Fritzing sketch OpenMQTTgateway_ESP32_Addon_RF (saved by Fritzing 0.9.10b)
breadboards: 1

parts:
  U6 = RF-LINK_TX [package=rf-link_tx]
  U7 = RF-LINK_RX [package=rf-link_rx]
  V1 = DC Power [voltage=5]
  Composant1 = Adafruit HUZZAH32 ESP32 Feather [part_number="Adafruit #3405"]

nets:
  N1: U6.DATA, Composant1.IO12_A11
  GND: U6.GND, U7.GND, Composant1.GND
  +5V: U6.+5V, U7.VCC, V1.V+, Composant1.3.3V
  N2: U7.Data#3, Composant1.IO27_A10

custom parts:
  RF-LINK_TX: Common RF transmitter of the 315.00Mhz varity
  RF-LINK_RX: RF Link receivers- WRL-8947, 8948, 8949, 8950
