# Fritzing sketch OpenMQTTgateway_ESP8266_Addon_I2C (saved by Fritzing 0.9.3b)
breadboards: 1

parts:
  U1 = NodeMCU V1.0
  V1 = DC Power [voltage=5]
  Composant2 = BME280 Breakout

nets:
  N1: U1.D1, Composant2.SCK/SCL
  N2: U1.D2, Composant2.SDI/SDA
  3V3: U1.3V3, Composant2.3.3V
  GND: U1.GND, V1.V-, Composant2.GND
  N3: U1.Vin, V1.V+

custom parts:
  NodeMCU V1.0: ESP8266 based NodeMCU
