# Fritzing sketch OpenMQTTgateway_Arduino_Addon_IR (saved by Fritzing 0.9.2b)
breadboards: 1

parts:
  V1 = DC Power [voltage=5]
  LED2 = LEDs [package=led10mm]
  R2 = Resistor [tolerance=±5% resistance=330 package="2512 [SMD]"]
  Q1 = TRANSISTOR_NPN [package=to-92-ammo]
  IR2 = TSOP312.., 314.. [package=THT]
  Bauteil1 = Arduino Uno (Rev3)
  R3 = Resistor [tolerance=±5% resistance=220 package="2512 [SMD]"]

nets:
  N1: V1.V+, LED2.C, IR2.Vs, Bauteil1.5V
  N2: LED2.A, R3.Pin_0
  N3: R2.Pin_0, Bauteil1.D9_PWM
  N4: R2.Pin_1, Q1.B
  N5: Q1.E, R3.Pin_1
  GND: Q1.C, IR2.GND, Bauteil1.GND
  N6: IR2.Data, Bauteil1.D2
