# Fritzing sketch OpenMQTTgateway_Arduino_Addon_RF (saved by Fritzing 0.9.3b)
breadboards: 1

parts:
  U6 = RF-LINK_TX [package=rf-link_tx]
  U7 = RF-LINK_RX [package=rf-link_rx]
  V1 = DC Power [voltage=5]
  Bauteil1 = Arduino Uno (Rev3)

nets:
  N1: U6.DATA, Bauteil1.D4
  GND: U6.GND, U7.GND, Bauteil1.GND
  +5V: U6.+5V, U7.VCC, V1.V+, Bauteil1.5V
  N2: U7.Data#3, Bauteil1.D3_PWM

custom parts:
  RF-LINK_TX: Common RF transmitter of the 315.00Mhz varity
  RF-LINK_RX: RF Link receivers- WRL-8947, 8948, 8949, 8950
