# Fritzing sketch OpenMQTTgateway_Arduino_AllInOne_IR-RF-BT-DHT (saved by Fritzing 0.9.3b)
breadboards: 1

parts:
  U6 = RF-LINK_TX [package=rf-link_tx]
  U7 = RF-LINK_RX [package=rf-link_rx]
  V1 = DC Power [voltage=5]
  LED2 = LEDs [package=led10mm]
  R2 = Resistor [tolerance=±5% resistance=330 package="2512 [SMD]"]
  Q1 = TRANSISTOR_NPN [package=to-92-ammo]
  IR2 = TSOP312.., 314.. [package=THT]
  Composant1 = Arduino Uno (Rev3)
  Composant2 = Bluetooth HM-10
  RHT2 = Humidity and Temperature Sensor RHT03

nets:
  N1: U6.DATA, Composant1.D4
  GND: U6.GND, U7.GND, Q1.E, IR2.GND, Composant1.GND, Composant2.GND, RHT2.GND_2
  VCC: U6.+5V, U7.VCC, V1.V+, LED2.C, IR2.Vs, Composant1.5V, Composant2.VCC, RHT2.Vcc
  N2: U7.Data, Composant1.D3_PWM
  N3: LED2.A, Q1.C
  N4: R2.Pin_0, Q1.B
  N5: R2.Pin_1, Composant1.D9_PWM
  N6: IR2.Data, Composant1.D2
  N7: Composant1.D8, RHT2.Data-signal
  N8: Composant1.D5_PWM, Composant2.TXD
  N9: Composant1.D6_PWM, Composant2.RXD

custom parts:
  RF-LINK_TX: Common RF transmitter of the 315.00Mhz varity
  RF-LINK_RX: RF Link receivers- WRL-8947, 8948, 8949, 8950
