# Fritzing sketch OpenMQTTgateway_ESP8266_Addon_2G (saved by Fritzing 0.9.3b)
breadboards: 1

parts:
  V1 = DC Power [voltage=5]  # not connected
  GSM_SIM_GPRS_A6_A1 = A6 module [package=THT]
  U2 = NodeMCU V1.0

nets:
  N1: GSM_SIM_GPRS_A6_A1.GND#1, U2.GND
  N2: GSM_SIM_GPRS_A6_A1.H_TXD, U2.D7
  N3: GSM_SIM_GPRS_A6_A1.H_RXD, U2.D6

custom parts:
  A6 module: Approximation of A6, a simple GSM module.
  NodeMCU V1.0: ESP8266 based NodeMCU
