# Fritzing sketch OpenMQTTgateway_ESP8266_Addon_BT (saved by Fritzing 0.9.2b)
breadboards: 1

parts:
  U1 = NodeMCU V1.0
  V1 = DC Power [voltage=5]
  Composant1 = Bluetooth HM-10

nets:
  GND: U1.GND, V1.V-, Composant1.GND
  N1: U1.D6, Composant1.TXD
  N2: U1.D7, Composant1.RXD
  VIN: U1.Vin, V1.V+, Composant1.VCC

custom parts:
  NodeMCU V1.0: ESP8266 based NodeMCU
