# Fritzing sketch OpenMQTTgateway_ESP8266_Addon_DHT (saved by Fritzing 0.9.3b)
breadboards: 1

parts:
  U1 = NodeMCU V1.0
  V1 = DC Power [voltage=5]
  RHT1 = Humidity and Temperature Sensor RHT03

nets:
  N1: U1.D3, RHT1.Data-signal
  N2: U1.GND, V1.V-, RHT1.GND_2
  VIN: U1.Vin, V1.V+, RHT1.Vcc

custom parts:
  NodeMCU V1.0: ESP8266 based NodeMCU
