# Fritzing sketch OpenMQTTgateway_ESP8266_Addon_IR (saved by Fritzing 0.9.2b)
breadboards: 1

parts:
  U1 = NodeMCU V1.0
  V1 = DC Power [voltage=5]
  LED2 = LEDs [package=led10mm]
  R2 = Resistor [tolerance=±5% resistance=330 package="2512 [SMD]"]
  Q1 = TRANSISTOR_NPN [package=to-92-ammo]
  IR2 = TSOP312.., 314.. [package=THT]
  R3 = Resistor [tolerance=±5% resistance=330 package="2512 [SMD]"]  # not connected
  R4 = Resistor [tolerance=±5% resistance=330 package="2512 [SMD]"]  # not connected
  R5 = Resistor [tolerance=±5% resistance=220 package="2512 [SMD]"]

nets:
  N1: U1.D0, R2.Pin_0
  N2: U1.D4, IR2.Data
  GND: U1.GND, V1.V-, Q1.C, IR2.GND
  N3: U1.Vin, V1.V+, LED2.C, IR2.Vs
  N4: LED2.A, R5.Pin_0
  N5: R2.Pin_1, Q1.B
  N6: Q1.E, R5.Pin_1

custom parts:
  NodeMCU V1.0: ESP8266 based NodeMCU
