# Fritzing sketch OpenMQTTgateway_ESP8266_Addon_RF (saved by Fritzing 0.9.3b)
breadboards: 1

parts:
  U1 = NodeMCU V1.0
  U6 = RF-LINK_TX [package=rf-link_tx]
  U7 = RF-LINK_RX [package=rf-link_rx]
  V1 = DC Power [voltage=5]

nets:
  GND: U1.GND, U6.GND, U7.GND, V1.V-
  N1: U1.D8, U6.DATA
  N2: U1.RX, U7.Data#3
  VIN: U1.Vin, U6.+5V, U7.VCC, V1.V+

custom parts:
  NodeMCU V1.0: ESP8266 based NodeMCU
  RF-LINK_TX: Common RF transmitter of the 315.00Mhz varity
  RF-LINK_RX: RF Link receivers- WRL-8947, 8948, 8949, 8950
