# Fritzing sketch OpenMQTTgateway_ESP8266_Addon_RFM69 (saved by Fritzing 0.9.3b)
breadboards: 1

parts:
  U1 = NodeMCU V1.0
  V1 = DC Power [voltage=5]
  RFM1 = RFM69HCW ISM Transciever
  ANT1 = Antenna

nets:
  N1: U1.D1, RFM1.5_NSS_(CS)
  N2: U1.3V3, RFM1.13_3.3V
  N3: U1.GND, V1.V-, RFM1.10_GND
  N4: U1.D5, RFM1.4_SCK
  N5: U1.D6, RFM1.2_MISO
  N6: U1.D7, RFM1.3_MOSI
  N7: U1.D8, RFM1.14_DIO0
  N8: U1.Vin, V1.V+
  N9: RFM1.9_ANT, ANT1.antenna_lead

custom parts:
  NodeMCU V1.0: ESP8266 based NodeMCU
  RFM69HCW ISM Transciever: RF Transceiver by Hope RF. Well supported Arduino libraries are available. This ISM band transceiver is available in several frequencies e.g. 433MHz and 915MHz and it is also available in various feature versions.
