# Fritzing sketch openmqttgateway_I2C (saved by Fritzing 0.9.2b)
breadboards: 1

parts:
  U1 = NodeMCU V1.0
  U6 = RF-LINK_TX [package=rf-link_tx]
  U7 = RF-LINK_RX [package=rf-link_rx]
  V1 = DC Power [voltage=5]  # not connected
  LED2 = LEDs [package=led10mm]
  R2 = Resistor [tolerance=±5% resistance=330 package="2512 [SMD]"]
  Q1 = TRANSISTOR_NPN [package=to-92-ammo]
  IR2 = TSOP312.., 314.. [package=THT]
  Composant2 = BME280 Breakout

nets (from the breadboard view):
  N1: U1.D0, R2.Pin_1
  N2: U1.D1, Composant2.SCK/SCL
  N3: U1.D2, Composant2.SDI/SDA
  N4: U1.D3, U7.Data
  N5: U1.D4, IR2.Data
  3V3: U1.3V3, Composant2.3.3V
  GND: U1.GND, U6.GND, U7.GND, Q1.E, IR2.GND, Composant2.GND
  N6: U1.D8, U6.DATA
  VIN: U1.Vin, U6.+5V, U7.VCC, LED2.C, IR2.Vs
  N7: LED2.A, Q1.C
  N8: R2.Pin_0, Q1.B

custom parts:
  NodeMCU V1.0: ESP9266 based NodeMCU
  RF-LINK_TX: Common RF transmitter of the 315.00Mhz varity
  RF-LINK_RX: RF Link receivers- WRL-8947, 8948, 8949, 8950
