# Fritzing sketch openmqttgateway_IR_RF_BT (saved by Fritzing 0.9.2b)
breadboards: 1

parts:
  U1 = NodeMCU V1.0
  U6 = RF-LINK_TX [package=rf-link_tx]
  U7 = RF-LINK_RX [package=rf-link_rx]
  V1 = DC Power [voltage=5]
  LED2 = LEDs [package=led10mm]
  R2 = Resistor [tolerance=±5% resistance=330 package="2512 [SMD]"]
  Q1 = TRANSISTOR_NPN [package=to-92-ammo]
  IR2 = TSOP312.., 314.. [package=THT]
  Composant1 = Bluetooth HM-10

nets:
  N1: U1.D1, U7.Data
  N2: U1.D2, U6.DATA
  N3: U1.D4, IR2.Data
  GND: U1.GND, U6.GND, U7.GND, V1.V-, Q1.E, IR2.GND, Composant1.GND
  N4: U1.D5, R2.Pin_1
  N5: U1.D6, Composant1.RXD
  N6: U1.D7, Composant1.TXD
  VCC: U1.Vin, U6.+5V, U7.VCC, V1.V+, LED2.C, IR2.Vs, Composant1.VCC
  N7: LED2.A, Q1.C
  N8: R2.Pin_0, Q1.B

custom parts:
  NodeMCU V1.0: ESP9266 based NodeMCU
  RF-LINK_TX: Common RF transmitter of the 315.00Mhz varity
  RF-LINK_RX: RF Link receivers- WRL-8947, 8948, 8949, 8950
