# Fritzing sketch openmqttgateway_RFM69 (saved by Fritzing 0.9.2b)
breadboards: 1

parts:
  U1 = NodeMCU V1.0
  U6 = RF-LINK_TX [package=rf-link_tx]
  U7 = RF-LINK_RX [package=rf-link_rx]
  V1 = DC Power [voltage=5]  # not connected
  LED2 = LEDs [package=led10mm]
  R2 = Resistor [tolerance=±5% resistance=330 package="2512 [SMD]"]
  Q1 = TRANSISTOR_NPN [package=to-92-ammo]
  IR2 = TSOP312.., 314.. [package=THT]
  RFM1 = RFM69HCW ISM Transciever
  ANT1 = Antenna

nets (from the breadboard view):
  N1: U1.D0, R2.Pin_1
  N2: U1.D1, RFM1.5_NSS_(CS)
  N3: U1.D3, U7.Data
  N4: U1.D4, IR2.Data
  N5: U1.3V3, RFM1.13_3.3V
  GND: U1.GND, U6.GND, U7.GND, Q1.E, IR2.GND, RFM1.10_GND
  N6: U1.D5, RFM1.4_SCK
  N7: U1.D6, RFM1.2_MISO
  N8: U1.D7, RFM1.3_MOSI
  N9: U1.D8, RFM1.14_DIO0
  VIN: U1.Vin, U6.+5V, U7.VCC, LED2.C, IR2.Vs
  N10: U1.SD3, U6.DATA
  N11: LED2.A, Q1.C
  N12: R2.Pin_0, Q1.B
  N13: RFM1.9_ANT, ANT1.antenna_lead

custom parts:
  NodeMCU V1.0: ESP9266 based NodeMCU
  RF-LINK_TX: Common RF transmitter of the 315.00Mhz varity
  RF-LINK_RX: RF Link receivers- WRL-8947, 8948, 8949, 8950
  RFM69HCW ISM Transciever: RF Transceiver by Hope RF. Well supported Arduino libraries are available. This ISM band transceiver is available in several frequencies e.g. 433MHz and 915MHz and it is also available in various feature versions.
